# Fritzing sketch TableSoccer (saved by Fritzing 0.9.0b)
breadboards: 2

parts:
  Part1 = Arduino Uno (Rev3) - ICSP
  LCD1 = LCD screen
  R7 = Trimmer Potentiometer [maximum_resistance=10kΩ package=THT]
  S1 = Pushbutton [package="[THT]"]
  S2 = Pushbutton [package="[THT]"]
  S3 = Pushbutton [package="[THT]"]
  S4 = Pushbutton [package="[THT]"]
  R8 = Resistor [tolerance=±5% resistance=1k package=THT]
  R9 = Resistor [tolerance=±5% resistance=1k package=THT]
  R10 = Resistor [tolerance=±5% resistance=1k package=THT]
  R11 = Resistor [tolerance=±5% resistance=1k package=THT]

nets:
  N1: Part1.A0, R8.Pin_0
  N2: Part1.D8, LCD1.E
  N3: Part1.D9_PWM, LCD1.DB4
  N4: Part1.D10_PWM/SS, LCD1.DB5
  N5: Part1.D11_PWM/MOSI, LCD1.DB6
  N6: Part1.D12/MISO, LCD1.DB7
  N7: Part1.D7, LCD1.RS
  5V: Part1.5V, LCD1.VDD, LCD1.LED+, R7.leg1
  GND: Part1.GND, LCD1.VSS, LCD1.R/W, LCD1.LED-, R7.leg2, S1.Pin_3, S1.Pin_4, S2.Pin_3, S2.Pin_4, S3.Pin_3, S3.Pin_4, S4.Pin_3, S4.Pin_4
  N8: LCD1.V0, R7.wiper
  N9: S1.Pin_1, S1.Pin_2, R8.Pin_1, R9.Pin_0
  N10: S2.Pin_1, S2.Pin_2, R9.Pin_1, R10.Pin_0
  N11: S3.Pin_1, S3.Pin_2, R10.Pin_1, R11.Pin_0
  N12: S4.Pin_1, S4.Pin_2, R11.Pin_1
